# Fritzing sketch TDA1543_Test (saved by Fritzing 0.9.2b)
breadboards: 1
perfboards: 1

parts:
  U1 = mystery part, 8 pins [chip_label=TDA1543]
  J1 = female pin header, 26 pins [form="♀ (female)"]  # not connected
  J1_2 = female pin header, 26 pins [form="♀ (female)"]
  J2 = female pin header, 7 pins [form="♀ (female)"]  # not connected
  J3 = female pin header, 7 pins [form="♀ (female)"]  # not connected
  C1 = Ceramic Capacitor [capacitance=100nF package="100 mil [THT, multilayer]"]
  R1 = Resistor [tolerance=±5% resistance=1.5k package=THT]
  R2 = Resistor [tolerance=±5% resistance=2.2k package=THT]
  R3 = Resistor [tolerance=±5% resistance=2.2k package=THT]
  C2 = Electrolytic Capacitor [capacitance=1µF package="100 mil [THT, electrolytic]"]
  Power_plug1 = Power plug

nets:
  N1: U1.pin1, J1_2.pin26
  N2: U1.pin2, J1_2.pin24
  N3: U1.pin3, J1_2.pin25
  N4: U1.pin4, J1_2.pin2, C1.1, R1.Pin_0, R2.Pin_0, R3.Pin_0, C2.-, Power_plug1.GND
  N5: U1.pin5, C1.0, C2.+, Power_plug1.VCC
  N6: U1.pin6, R3.Pin_1
  N7: U1.pin7, R1.Pin_1
  N8: U1.pin8, R2.Pin_1

notes:
  TDA1543
  1.BCK 8.AOR
  2.WS 7.Vref
  3.DATA 6.AOL
  4.GND 5.VDD
  ROUT
  LOUT
  PSoC 5LP Prototyping Kit
  可変電圧源
